# Fritzing sketch TapuinoNext (saved by Fritzing 0.9.7b)
circuit board: 8.46667cm x 5.64444cm
breadboards: 1

parts:
  microSD_Transflash1 = SparkFun - microSD Transflash
  OLED_I2C1 = OLED 128x64 I2C Monochrome Display
  U1 = ESP32-38PinWide [part_number=ESP32-38PinWide]
  JP1 = Header 6 [package=1x06_smd_straight_alt]
  RE1 = KY-040 Rotary encoder [package=THT]
  R4 = Resistor [tolerance=±5% resistance=3.3k power=0.25 package=THT]
  Part2 = I2C level shifter bidirectional
  R3 = Resistor [tolerance=±5% resistance=1.5k power=0.25 package=THT]

nets:
  N1: microSD_Transflash1.DO, U1.GPIO2
  GND: microSD_Transflash1.GND, microSD_Transflash1.CS, OLED_I2C1.GND, U1.GND, JP1.1, RE1.GND, R4.Pin_0, Part2.GND
  N2: microSD_Transflash1.SCK, U1.GPIO14
  VCC: microSD_Transflash1.VCC, U1.3.3, RE1.Vcc, Part2.LV
  N3: microSD_Transflash1.DI, U1.GPIO15
  N4: OLED_I2C1.SDA, U1.GPIO21
  N5: OLED_I2C1.SCK, U1.GPIO22
  VDD: OLED_I2C1.VDD, U1.VIN, JP1.2, Part2.HV
  N6: U1.GPIO32, RE1.SW
  N7: U1.GPIO33, RE1.DT
  N8: U1.GPIO25, RE1.CLK
  N9: U1.GPIO16, Part2.LV1
  N10: U1.GPIO17, Part2.LV2
  N11: U1.GPIO5, Part2.LV3
  N12: U1.GPIO18, Part2.LV4
  N13: JP1.3, R3.Pin_1
  N14: JP1.4, Part2.HV3
  N15: JP1.5, Part2.HV4
  N16: JP1.6, Part2.HV1
  N17: R4.Pin_1, Part2.HV2, R3.Pin_0

notes:
  C64 TAPE Connector
  1. Black => C64 Datasette GND
  2. Red => C64 Datasette 5V
  3. Pink => C64 Datasette Motor
  4. Yellow => C64 Datasette Read
  5. White => C64 Datasette Write
  6. Blue => C64 Datasette Sense
  +5V Red wire
  +3.3V Orange wire
  v0.3
  Original by Attila Gabriel, fixes by sweetlilmre

custom parts:
  ESP32-38PinWide: Generic 38-Pin ESP32 with wide format (only access to one side of pins on a breadboard) based on Stephen Lilley's HiLetgo ESP-WROOM-32 ESP32 ESP-32S Development Board.
  KY-040 Rotary encoder: KY-040 Rotary Encoder with switch on breakout borad from AZ Delivery
